// Logisim project ALU.circ as structural Verilog: 1 circuit, main circuit ALU
module ALU (
  input  [31:0] A,
  input  [31:0] B,
  input  [4:0] Shift,
  input  [3:0] Codop,
  input  CarryIn,
  output [31:0] S,
  output [3:0] Flags
);

  wire ADC_Cout, and_3_out, and_4_out, and_5_out, and_6_out, bitselector_1_out, bitselector_2_out, CMN_Cout,
       CMP_Cout, comparator_1_gt, comparator_2_lt, comparator_3_gt, comparator_4_gt, comparator_5_eq,
       not_2_out, or_2_out, or_3_out, RSB_Cout, SBC_Cout, subtractor_1_bout, subtractor_2_bout,
       subtractor_3_bout;
  wire [4:0] subtractor_4_out, subtractor_5_out;
  wire [31:0] adder_1_out, and_2_out, CMN, CMP, multiplexer_2_out, multiplier_1_out, not_1_out, not_3_out,
       or_1_out, shifter_1_out, shifter_2_out, shifter_3_out, shifter_4_out, subtractor_1_out,
       subtractor_2_out, TST, xor_1_out;

  assign not_1_out = ~A;  // NOT_Gate not_1, 32 bits wide
  assign TST = A & B;  // AND_Gate and_1, 32 bits wide
  assign xor_1_out = B ^ A;  // XOR_Gate xor_1, 32 bits wide
  Shifter #(.width(32)) shifter_1 (.in(B), .\dist (Shift), .out(shifter_1_out));
  Shifter #(.shift("lr"), .width(32)) shifter_2 (.in(B), .\dist (Shift), .out(shifter_2_out));
  Shifter #(.shift("ar"), .width(32)) shifter_3 (.in(B), .\dist (Shift), .out(shifter_3_out));
  Adder #(.width(32)) adder_1 (.a(A), .b(B), .out(adder_1_out), .cin(CarryIn), .cout(ADC_Cout));
  not not_2 (not_2_out, CarryIn);
  Subtractor #(.width(32)) subtractor_1 (
    .a(B), .b(A), .out(subtractor_1_out), .bin(not_2_out), .bout(subtractor_1_bout));
  Shifter #(.shift("rr"), .width(32)) shifter_4 (.in(B), .\dist (Shift), .out(shifter_4_out));
  Subtractor #(.width(32)) subtractor_2 (
    .a({32{1'b0}}), .b(A), .out(subtractor_2_out), .bout(subtractor_2_bout));  // open: bin
  Subtractor #(.width(32)) subtractor_3 (.a(B), .b(A), .out(CMP), .bout(subtractor_3_bout));  // open: bin
  Adder #(.width(32)) adder_2 (.a(A), .b(B), .out(CMN), .cout(CMN_Cout));  // open: cin
  assign or_1_out = B | A;  // OR_Gate or_1, 32 bits wide
  Multiplier #(.width(32)) multiplier_1 (.a(A), .b(B), .out(multiplier_1_out));  // open: cin, cout
  assign and_2_out = B & not_1_out;  // AND_Gate and_2, 32 bits wide
  assign not_3_out = ~A;  // NOT_Gate not_3, 32 bits wide
  not not_4 (SBC_Cout, subtractor_1_bout);
  not not_5 (RSB_Cout, subtractor_2_bout);
  not not_6 (CMP_Cout, subtractor_3_bout);
  Multiplexer #(.select(4), .width(32)) multiplexer_1 (
    .in0(TST), .in1(xor_1_out), .in2(shifter_1_out), .in3(shifter_2_out), .in4(shifter_3_out),
    .in5(adder_1_out), .in6(subtractor_1_out), .in7(shifter_4_out), .in8(B), .in9(subtractor_2_out),
    .in10(B), .in11(B), .in12(or_1_out), .in13(multiplier_1_out), .in14(and_2_out), .in15(not_3_out),
    .out(S), .sel(Codop));
  Subtractor #(.width(5)) subtractor_4 (.a({5{1'b0}}), .b(Shift), .out(subtractor_4_out));  // open: bin, bout
  Subtractor #(.width(5)) subtractor_5 (.a(Shift), .b(5'b00001), .out(subtractor_5_out));  // open: bin, bout
  Comparator #(.width(32)) comparator_1 (.a({32{1'b0}}), .b(B), .gt(comparator_1_gt));  // open: eq, lt
  Comparator #(.width(32)) comparator_2 (.a(A), .b({32{1'b0}}), .lt(comparator_2_lt));  // open: gt, eq
  Comparator #(.width(32)) comparator_3 (.a({32{1'b0}}), .b(B), .gt(comparator_3_gt));  // open: eq, lt
  Comparator #(.width(32)) comparator_4 (.a({32{1'b0}}), .b(A), .gt(comparator_4_gt));  // open: eq, lt
  BitSelector #(.width(32)) bitselector_1 (.in(B), .out(bitselector_1_out), .sel(subtractor_4_out));
  BitSelector #(.width(32)) bitselector_2 (.in(B), .out(bitselector_2_out), .sel(subtractor_5_out));
  and and_3 (and_3_out, ~comparator_1_gt, ~comparator_2_lt, Flags[3]);  // AND_Gate
  or or_2 (or_2_out, and_3_out, and_4_out);
  and and_4 (and_4_out, ~Flags[3], comparator_1_gt, comparator_2_lt);  // AND_Gate
  Comparator #(.width(32)) comparator_5 (.a(A), .b(32'h80000000), .eq(comparator_5_eq));  // open: gt, lt
  and and_5 (and_5_out, ~comparator_3_gt, comparator_4_gt, Flags[3]);  // AND_Gate
  or or_3 (or_3_out, and_5_out, and_6_out);
  and and_6 (and_6_out, ~Flags[3], comparator_3_gt, ~comparator_4_gt);  // AND_Gate
  Multiplexer #(.select(4), .width(32)) multiplexer_2 (
    .in0(S), .in1(S), .in2(S), .in3(S), .in4(S), .in5(S), .in6(S), .in7(S), .in8(TST), .in9(S), .in10(CMP),
    .in11(CMN), .in12(S), .in13(S), .in14(S), .in15(S), .out(multiplexer_2_out), .sel(Codop));
  Comparator #(.width(32)) comparator_6 (
    .a(multiplexer_2_out), .b({32{1'b0}}), .eq(Flags[2]), .lt(Flags[3]));  // open: gt
  Multiplexer #(.select(4)) multiplexer_3 (
    .in0(1'b0), .in1(1'b0), .in2(bitselector_1_out), .in3(bitselector_2_out), .in4(bitselector_2_out),
    .in5(ADC_Cout), .in6(SBC_Cout), .in7(Flags[3]), .in8(1'b0), .in9(RSB_Cout), .in10(CMP_Cout),
    .in11(CMN_Cout), .in12(1'b0), .in13(1'b0), .in14(1'b0), .in15(1'b0), .out(Flags[1]), .sel(Codop));
  Multiplexer #(.select(4)) multiplexer_4 (
    .in0(1'b0), .in1(1'b0), .in2(1'b0), .in3(1'b0), .in4(1'b0), .in5(or_2_out), .in6(or_3_out), .in7(1'b0),
    .in8(1'b0), .in9(comparator_5_eq), .in10(or_3_out), .in11(or_2_out), .in12(1'b0), .in13(1'b0),
    .in14(1'b0), .in15(1'b0), .out(Flags[0]), .sel(Codop));

  // Other names for the same wires on the sheet: Cin = CarryIn; V = Flags[0]; C = Flags[1]; Z = Flags[2];
  //   N = Flags[3]; Result[31:0] = S

  // Notes on the sheet:
  //   Note: for ROR, C = N
  //   Note 2: assume that shift > 0 for LSL and LSR
endmodule
