// Logisim project Ctl_Conditional.circ as structural Verilog: 1 circuit, main circuit Conditional
module Conditional (
  input  Enable,
  input  [15:0] Instruction,
  input  Z,
  input  C,
  input  N,
  input  V,
  output [10:0] Offset,
  output Verified
);

  wire and_1_out, and_2_out, and_3_out, and_4_out, and_5_out, and_6_out, and_7_out, and_8_out, and_9_out,
       and_10_out, and_11_out, and_12_out, and_13_out, and_14_out, and_15_out, and_16_out, decoder_1_out0,
       decoder_1_out1, decoder_1_out2, decoder_1_out3, decoder_1_out4, decoder_1_out5, decoder_1_out6,
       decoder_1_out7, decoder_1_out8, decoder_1_out9, decoder_1_out10, decoder_1_out11, decoder_1_out12,
       decoder_1_out13, decoder_1_out14, decoder_1_out15, multiplexer_3_out, multiplexer_4_out, not_1_out,
       not_2_out, not_3_out, not_4_out, not_5_out, not_6_out, not_7_out, not_8_out, or_1_out, or_2_out,
       xnor_1_out, xor_1_out;
  wire [10:0] multiplexer_1_out;

  Decoder #(.select(4)) decoder_1 (
    .out0(decoder_1_out0), .out1(decoder_1_out1), .out2(decoder_1_out2), .out3(decoder_1_out3),
    .out4(decoder_1_out4), .out5(decoder_1_out5), .out6(decoder_1_out6), .out7(decoder_1_out7),
    .out8(decoder_1_out8), .out9(decoder_1_out9), .out10(decoder_1_out10), .out11(decoder_1_out11),
    .out12(decoder_1_out12), .out13(decoder_1_out13), .out14(decoder_1_out14), .out15(decoder_1_out15),
    .sel(Instruction[11:8]));  // open: en
  not not_1 (not_1_out, Z);
  not not_2 (not_2_out, C);
  not not_3 (not_3_out, Z);
  not not_4 (not_4_out, C);
  not not_5 (not_5_out, Z);
  not not_6 (not_6_out, N);
  Multiplexer #(.width(11)) multiplexer_1 (
    .in0({Instruction[7:0], 3'b111}), .in1(Instruction[10:0]), .out(multiplexer_1_out), .sel(Instruction[13]));
  not not_7 (not_7_out, V);
  and and_1 (and_1_out, C, not_3_out);
  or or_1 (or_1_out, Z, not_4_out);
  xnor xnor_1 (xnor_1_out, N, V);
  xor xor_1 (xor_1_out, N, V);
  Multiplexer #(.width(11)) multiplexer_2 (.in0({11{1'b0}}), .in1(multiplexer_1_out), .out(Offset), .sel(Enable));
  and and_2 (and_2_out, Z, decoder_1_out0);
  and and_3 (and_3_out, decoder_1_out1, not_1_out);
  and and_4 (and_4_out, C, decoder_1_out2);
  and and_5 (and_5_out, not_2_out, decoder_1_out3);
  and and_6 (and_6_out, N, decoder_1_out4);
  and and_7 (and_7_out, not_6_out, decoder_1_out5);
  and and_8 (and_8_out, V, decoder_1_out6);
  and and_9 (and_9_out, not_7_out, decoder_1_out7);
  and and_10 (and_10_out, and_1_out, decoder_1_out8);
  and and_11 (and_11_out, or_1_out, decoder_1_out9);
  and and_12 (and_12_out, not_5_out, xnor_1_out);
  or or_2 (or_2_out, xor_1_out, Z);
  not not_8 (not_8_out, decoder_1_out15);
  and and_13 (and_13_out, xnor_1_out, decoder_1_out10);
  and and_14 (and_14_out, xor_1_out, decoder_1_out11);
  and and_15 (and_15_out, and_12_out, decoder_1_out12);
  and and_16 (and_16_out, or_2_out, decoder_1_out13);
  Multiplexer #(.select(4)) multiplexer_3 (
    .in0(and_2_out), .in1(and_3_out), .in2(and_4_out), .in3(and_5_out), .in4(and_6_out), .in5(and_7_out),
    .in6(and_8_out), .in7(and_9_out), .in8(and_10_out), .in9(and_11_out), .in10(and_13_out),
    .in11(and_14_out), .in12(and_15_out), .in13(and_16_out), .in14(decoder_1_out14), .in15(not_8_out),
    .out(multiplexer_3_out), .sel(Instruction[11:8]));
  Multiplexer multiplexer_4 (.in0(multiplexer_3_out), .in1(1'b1), .out(multiplexer_4_out), .sel(Instruction[13]));
  and and_17 (Verified, multiplexer_4_out, Enable);

  // Other names for the same wires on the sheet: imm8[7:0] = Instruction[7:0]; imm11[10:0] = Instruction[10:0];
  //   condition[3:0] = Instruction[11:8]; bit_13 = Instruction[13]
endmodule
